# Fritzing sketch shema (saved by Fritzing 0.9.3b)
breadboards: 1

parts:
  Button = Pushbutton [package="[SMD]"]
  Potentiometer = Rotary Potentiometer (Small) [maximum_resistance=100kΩ package=THT]
  RGB_LED = RGB LED (com. cathode, rgb) [package="5 mm [THT]"]
  Composant1 = Arduino Uno (Rev3)
  R1 = Resistor [tolerance=±5% resistance=220 package=THT]
  R2 = Resistor [tolerance=±5% resistance=220 package=THT]
  R3 = Resistor [tolerance=±5% resistance=220 package=THT]
  R4 = Resistor [tolerance=±5% resistance=220 package=THT]

nets:
  N1: Button.Pin_1, Button.Pin_2, Composant1.D13/SCK, R4.Pin_0
  N2: Button.Pin_3, Button.Pin_4, Potentiometer.leg2, Composant1.5V
  N3: Potentiometer.leg1, RGB_LED.common_cathode, Composant1.GND, R4.Pin_1
  N4: Potentiometer.wiper, Composant1.A0
  N5: RGB_LED.red_anode, Composant1.D3_PWM, R3.Pin_1
  N6: RGB_LED.green_anode, R2.Pin_1
  N7: RGB_LED.blue_anode, R1.Pin_1
  N8: Composant1.D5_PWM, R2.Pin_0
  N9: Composant1.D6_PWM, R1.Pin_0
